# Fritzing sketch Temperature_Detection_Arduino_UNO (saved by Fritzing 0.9.3b)
breadboards: 1

parts:
  V1 = DC Power [voltage=5]  # not connected
  Bauteil1 = Arduino Uno (Rev3)
  hc-sr1 = hc-sr04
  U1 = MLX90614 [package=to-39]
  R1 = Resistor [tolerance=±5% resistance=4.7k package="0603 [SMD]"]
  R2 = Resistor [tolerance=±5% resistance=4.7k package="0603 [SMD]"]
  LED3 = LED - 3mm [color="Green (560nm)" package="3 mm [THT]"]
  LED2 = LED - 3mm [color="Orange (620nm)" package="3 mm [THT]"]
  LED1 = LED - 3mm [color="Red (633nm)" package="3 mm [THT]"]
  R3 = Resistor [tolerance=±5% resistance=470 package="0603 [SMD]"]
  R4 = Resistor [tolerance=±5% resistance=470 package="0603 [SMD]"]
  R5 = Resistor [tolerance=±5% resistance=470 package="0603 [SMD]"]

nets:
  N1: Bauteil1.A4/SDA, U1.PWM_SDA, R1.Pin_0
  N2: Bauteil1.A5/SCL, U1.SCL_VZ, R2.Pin_0
  GND: Bauteil1.GND, hc-sr1.GND, U1.VSS, LED1.anode, R5.Pin_0
  N3: Bauteil1.D2, hc-sr1.Trig
  N4: Bauteil1.D3_PWM, hc-sr1.Echo
  N5: Bauteil1.D4, R3.Pin_1
  N6: Bauteil1.D5_PWM, R4.Pin_1
  N7: Bauteil1.D6_PWM, R5.Pin_1
  3V3: Bauteil1.3V3, U1.VDD, R1.Pin_1, R2.Pin_1
  5V: Bauteil1.5V, hc-sr1.VCC
  N8: LED3.cathode, LED2.cathode, LED1.cathode
  N9: LED3.anode, R3.Pin_0
  N10: LED2.anode, R4.Pin_0
